// Logisim project HW4.circ as structural Verilog: 12 circuits, main circuit main
module main (
);

  wire alu_1_zeros, and_1_out, clock_1_out, cu_1_alu_src, cu_1_mem_write, cu_1_reg_dst, cu_1_reg_write;
  wire [1:0] cu_1_alu_op;
  wire [2:0] multiplexer_1_out;
  wire [15:0] adder_1_out, adder_2_out, alu_1_alu_out, bit_extender_1_out, InstructionMemory_dout,
       multiplexer_2_out, multiplexer_3_out, multiplexer_4_out, PC_q, ram_1_dout, register_file_1_d1,
       register_file_1_d2, shifter_1_out;

  Clock clock_1 (.out(clock_1_out));
  RAM #(.addrWidth(16), .dataWidth(16)) InstructionMemory (
    .addr(PC_q), .clk(clock_1_out), .dout(InstructionMemory_dout));  // open: we, oe, din
  Register #(.width(16)) PC (.D(multiplexer_3_out), .en(1'b1), .Q(PC_q), .clk(clock_1_out));  // open: clr
  Adder #(.width(16)) adder_1 (.a(16'h1), .b(PC_q), .out(adder_1_out));  // open: cin, cout
  CU cu_1 (
    .in_1(InstructionMemory_dout[15:12]), .Reg_Dst(cu_1_reg_dst), .BranchOut(cu_1_reg_dst),
    .Mem_Read(cu_1_reg_dst), .Mem_To_Reg(cu_1_reg_dst), .ALU_Op(cu_1_alu_op), .Mem_Write(cu_1_mem_write),
    .ALU_Src(cu_1_alu_src), .Reg_Write(cu_1_reg_write));
  Multiplexer #(.enable("true"), .width(3)) multiplexer_1 (
    .in0(InstructionMemory_dout[10:8]), .in1(InstructionMemory_dout[4:2]), .out(multiplexer_1_out),
    .sel(cu_1_reg_dst));  // open: en
  assign bit_extender_1_out = {{10{InstructionMemory_dout[10]}}, InstructionMemory_dout[10:5]};  // Bit_Extender bit_extender_1
  Register_File register_file_1 (
    .W(cu_1_reg_write), .read2(InstructionMemory_dout[10:8]), .read1(InstructionMemory_dout[7:5]),
    .reg_W(multiplexer_1_out), .d_W(multiplexer_4_out), .clk(clock_1_out), .d1(register_file_1_d1),
    .d2(register_file_1_d2));  // open: reset
  Multiplexer #(.enable("true"), .width(16)) multiplexer_2 (
    .in0(register_file_1_d2), .in1(bit_extender_1_out), .out(multiplexer_2_out), .sel(cu_1_alu_src), .en(1'b1));
  Shifter #(.width(16)) shifter_1 (.in(bit_extender_1_out), .\dist (4'b0001), .out(shifter_1_out));
  ALU alu_1 (
    .A(register_file_1_d1), .B(multiplexer_2_out), .ALU_Control(cu_1_alu_op), .ALU_out(alu_1_alu_out),
    .Zeros(alu_1_zeros));
  // Probe on adder_1_out
  Adder #(.width(16)) adder_2 (.a(adder_1_out), .b(shifter_1_out), .out(adder_2_out));  // open: cin, cout
  and and_1 (and_1_out, cu_1_reg_dst, alu_1_zeros);
  RAM #(.addrWidth(16), .dataWidth(16)) ram_1 (
    .addr(alu_1_alu_out), .we(cu_1_mem_write), .oe(cu_1_reg_dst), .clk(clock_1_out), .dout(ram_1_dout));  // open: din
  Multiplexer #(.enable("true"), .width(16)) multiplexer_3 (
    .in0(adder_1_out), .in1(adder_2_out), .out(multiplexer_3_out), .sel(and_1_out), .en(1'b1));
  // Probe on ram_1_dout
  Multiplexer #(.enable("true"), .width(16)) multiplexer_4 (
    .in0(alu_1_alu_out), .in1(ram_1_dout), .out(multiplexer_4_out), .sel(cu_1_reg_dst));  // open: en
endmodule

module ALU (
  input  [15:0] A,
  input  [15:0] B,
  input  [1:0] ALU_Control,
  output [15:0] ALU_out,
  output Zeros
);

  wire or_2_out, or_3_out, or_4_out, or_5_out, or_6_out, or_7_out, or_8_out, or_9_out, or_10_out, or_11_out,
       or_12_out, or_13_out, or_14_out, or_15_out, or_16_out;
  wire [15:0] adder_1_out, and_1_out, or_1_out, subtractor_1_out;

  Adder #(.width(16)) adder_1 (.a(A), .b(B), .out(adder_1_out));  // open: cin, cout
  Subtractor #(.width(16)) subtractor_1 (.a(A), .b(B), .out(subtractor_1_out));  // open: bin, bout
  assign and_1_out = A & B;  // AND_Gate and_1, 16 bits wide
  assign or_1_out = A | B;  // OR_Gate or_1, 16 bits wide
  Multiplexer #(.enable("true"), .select(2), .width(16)) multiplexer_1 (
    .in0(adder_1_out), .in1(and_1_out), .in2(or_1_out), .in3(subtractor_1_out), .out(ALU_out),
    .sel(ALU_Control), .en(1'b1));
  or or_2 (or_2_out, ALU_out[0], ALU_out[1]);
  or or_3 (or_3_out, ALU_out[2], ALU_out[3]);
  or or_4 (or_4_out, ALU_out[4], ALU_out[5]);
  or or_5 (or_5_out, ALU_out[6], ALU_out[7]);
  or or_6 (or_6_out, ALU_out[8], ALU_out[9]);
  or or_7 (or_7_out, ALU_out[10], ALU_out[11]);
  or or_8 (or_8_out, ALU_out[12], ALU_out[13]);
  or or_9 (or_9_out, ALU_out[14], ALU_out[15]);
  or or_10 (or_10_out, or_2_out, or_3_out);
  or or_11 (or_11_out, or_4_out, or_5_out);
  or or_12 (or_12_out, or_6_out, or_7_out);
  or or_13 (or_13_out, or_8_out, or_9_out);
  or or_14 (or_14_out, or_10_out, or_11_out);
  or or_15 (or_15_out, or_12_out, or_13_out);
  or or_16 (or_16_out, or_14_out, or_15_out);
  not not_1 (Zeros, or_16_out);
endmodule

module CU (
  input  [3:0] in_1,
  output Reg_Dst,
  output BranchOut,
  output Mem_Read,
  output Mem_To_Reg,
  output [1:0] ALU_Op,
  output Mem_Write,
  output ALU_Src,
  output Reg_Write
);

  RegDst regdst_1 (.OpCode(in_1), .Reg_Dst(Reg_Dst));
  Branch branch_1 (.OpCode(in_1), .Branch_Out(BranchOut));
  MemRead memread_1 (.OpCode(in_1), .Mem_Read(Mem_Read));
  MemToReg memtoreg_1 (.OpCode(in_1), .Mem_ToReg(Mem_To_Reg));
  ALUOp aluop_1 (.OpCode(in_1), .ALU_Op(ALU_Op));
  MemWrite memwrite_1 (.OpCode(in_1), .Mem_Write(Mem_Write));
  ALUSrc alusrc_1 (.OpCode(in_1), .ALU_Src(ALU_Src));
  RegWrite regwrite_1 (.OpCode(in_1), .Reg_Write(Reg_Write));
endmodule

module RegDst (
  input  [3:0] OpCode,
  output Reg_Dst
);

  wire A_NOT_C_out, and_1_out, and_2_out, and_3_out, and_4_out, not_1_out, not_2_out, not_3_out, or_1_out;

  not not_1 (not_1_out, OpCode[1]);
  not not_2 (not_2_out, OpCode[3]);
  and A_NOT_C (A_NOT_C_out, OpCode[3], not_1_out);
  and and_1 (and_1_out, not_2_out, OpCode[2]);
  and and_2 (and_2_out, OpCode[2], OpCode[1]);
  not not_3 (not_3_out, OpCode[0]);
  and and_3 (and_3_out, and_1_out, OpCode[1]);
  and and_4 (and_4_out, and_2_out, not_3_out);
  or or_1 (or_1_out, A_NOT_C_out, and_3_out);
  or or_2 (Reg_Dst, or_1_out, and_4_out);
endmodule

module ALUSrc (
  input  [3:0] OpCode,
  output ALU_Src
);

  wire and_1_out, and_2_out, and_3_out, and_4_out, and_5_out, and_6_out, not_1_out, not_2_out, not_3_out,
       or_1_out;

  not not_1 (not_1_out, OpCode[3]);
  and and_1 (and_1_out, not_1_out, OpCode[2]);
  and and_2 (and_2_out, OpCode[3], not_2_out);
  not not_2 (not_2_out, OpCode[2]);
  and and_3 (and_3_out, OpCode[3], OpCode[1]);
  and and_4 (and_4_out, and_1_out, OpCode[1]);
  and and_5 (and_5_out, and_2_out, not_3_out);
  not not_3 (not_3_out, OpCode[0]);
  and and_6 (and_6_out, and_3_out, OpCode[0]);
  or or_1 (or_1_out, and_4_out, and_5_out);
  or or_2 (ALU_Src, or_1_out, and_6_out);
endmodule

module MemToReg (
  input  [3:0] OpCode,
  output Mem_ToReg
);

  wire and_1_out;

  and and_1 (and_1_out, OpCode[3], OpCode[1]);
  and and_2 (Mem_ToReg, and_1_out, OpCode[0]);
endmodule

module RegWrite (
  input  [3:0] OpCode,
  output Reg_Write
);

  wire and_1_out, and_2_out, and_3_out, not_1_out, or_1_out;

  and and_1 (and_1_out, OpCode[2], OpCode[1]);
  and and_2 (and_2_out, OpCode[3], not_1_out);
  not not_1 (not_1_out, OpCode[1]);
  and and_3 (and_3_out, OpCode[3], OpCode[0]);
  or or_1 (or_1_out, and_1_out, and_2_out);
  or or_2 (Reg_Write, or_1_out, and_3_out);
endmodule

module MemRead (
  input  [3:0] OpCode,
  output Mem_Read
);

  wire and_1_out, and_2_out, not_1_out;

  not not_1 (not_1_out, OpCode[2]);
  and and_1 (and_1_out, OpCode[3], not_1_out);
  and and_2 (and_2_out, OpCode[1], OpCode[0]);
  and and_3 (Mem_Read, and_1_out, and_2_out);
endmodule

module MemWrite (
  input  [3:0] OpCode,
  output Mem_Write
);

  wire and_1_out, and_2_out, not_1_out, not_2_out;

  not not_1 (not_1_out, OpCode[2]);
  not not_2 (not_2_out, OpCode[0]);
  and and_1 (and_1_out, OpCode[3], not_1_out);
  and and_2 (and_2_out, OpCode[1], not_2_out);
  and and_3 (Mem_Write, and_1_out, and_2_out);
endmodule

module Branch (
  input  [3:0] OpCode,
  output Branch_Out
);

  wire and_1_out, not_1_out, not_2_out;

  not not_1 (not_1_out, OpCode[3]);
  and and_1 (and_1_out, not_1_out, OpCode[2]);
  not not_2 (not_2_out, OpCode[1]);
  and and_2 (Branch_Out, and_1_out, not_2_out);
endmodule

module Register_File (
  input  W,
  input  [2:0] read2,
  input  [2:0] read1,
  input  [2:0] reg_W,
  input  [15:0] d_W,
  input  clk,
  input  reset,
  output [15:0] d1,
  output [15:0] d2
);

  wire and_1_out, and_2_out, and_3_out, and_4_out, and_5_out, and_6_out, and_7_out, and_8_out,
       decoder_1_out0, decoder_1_out1, decoder_1_out2, decoder_1_out3, decoder_1_out4, decoder_1_out5,
       decoder_1_out6, decoder_1_out7;
  wire [15:0] r1_q, r2_q, r3_q, r4_q, r5_q, r6_q, r7_q, r8_q;

  Decoder #(.enable("false"), .select(3)) decoder_1 (
    .out0(decoder_1_out0), .out1(decoder_1_out1), .out2(decoder_1_out2), .out3(decoder_1_out3),
    .out4(decoder_1_out4), .out5(decoder_1_out5), .out6(decoder_1_out6), .out7(decoder_1_out7), .sel(reg_W));
  and and_1 (and_1_out, W, decoder_1_out0);
  and and_2 (and_2_out, W, decoder_1_out1);
  and and_3 (and_3_out, W, decoder_1_out2);
  and and_4 (and_4_out, W, decoder_1_out3);
  and and_5 (and_5_out, W, decoder_1_out4);
  and and_6 (and_6_out, W, decoder_1_out5);
  and and_7 (and_7_out, W, decoder_1_out6);
  and and_8 (and_8_out, W, decoder_1_out7);
  Register #(.trigger("falling"), .width(16)) r1 (.D(d_W), .en(and_1_out), .Q(r1_q), .clk(clk), .clr(reset));
  Register #(.trigger("falling"), .width(16)) r2 (.D(d_W), .en(and_2_out), .Q(r2_q), .clk(clk), .clr(reset));
  Register #(.trigger("falling"), .width(16)) r3 (.D(d_W), .en(and_3_out), .Q(r3_q), .clk(clk), .clr(reset));
  Register #(.trigger("falling"), .width(16)) r4 (.D(d_W), .en(and_4_out), .Q(r4_q), .clk(clk), .clr(reset));
  Register #(.trigger("falling"), .width(16)) r5 (.D(d_W), .en(and_5_out), .Q(r5_q), .clk(clk), .clr(reset));
  Register #(.trigger("falling"), .width(16)) r6 (.D(d_W), .en(and_6_out), .Q(r6_q), .clk(clk), .clr(reset));
  Register #(.trigger("falling"), .width(16)) r7 (.D(d_W), .en(and_7_out), .Q(r7_q), .clk(clk), .clr(reset));
  Register #(.trigger("falling"), .width(16)) r8 (.D(d_W), .en(and_8_out), .Q(r8_q), .clk(clk), .clr(reset));
  Multiplexer #(.enable("true"), .select(3), .width(16)) multiplexer_1 (
    .in0(r1_q), .in1(r2_q), .in2(r3_q), .in3(r4_q), .in4(r5_q), .in5(r6_q), .in6(r7_q), .in7(r8_q), .out(d2),
    .sel(read2));  // open: en
  Multiplexer #(.enable("true"), .select(3), .width(16)) multiplexer_2 (
    .in0(r1_q), .in1(r2_q), .in2(r3_q), .in3(r4_q), .in4(r5_q), .in5(r6_q), .in6(r7_q), .in7(r8_q), .out(d1),
    .sel(read1));  // open: en
endmodule

module ALUOp (
  input  [3:0] OpCode,
  output [1:0] ALU_Op
);

  wire and_1_out, and_2_out, and_3_out, and_4_out, and_5_out, and_6_out, and_7_out, and_8_out, and_9_out,
       and_10_out, not_1_out, not_2_out, not_3_out, not_4_out, not_5_out, not_6_out, not_7_out, not_8_out,
       or_2_out;

  and and_1 (and_1_out, OpCode[3], OpCode[2]);
  not not_1 (not_1_out, OpCode[3]);
  and and_2 (and_2_out, not_1_out, OpCode[2]);
  and and_3 (and_3_out, OpCode[2], not_2_out);
  not not_2 (not_2_out, OpCode[1]);
  not not_3 (not_3_out, OpCode[3]);
  and and_4 (and_4_out, not_3_out, OpCode[2]);
  not not_4 (not_4_out, OpCode[3]);
  and and_5 (and_5_out, not_4_out, OpCode[2]);
  not not_5 (not_5_out, OpCode[1]);
  not not_6 (not_6_out, OpCode[0]);
  not not_7 (not_7_out, OpCode[1]);
  not not_8 (not_8_out, OpCode[0]);
  and and_6 (and_6_out, and_1_out, not_5_out);
  and and_7 (and_7_out, and_2_out, OpCode[1]);
  and and_8 (and_8_out, and_3_out, not_6_out);
  and and_9 (and_9_out, and_4_out, not_7_out);
  and and_10 (and_10_out, and_5_out, not_8_out);
  or or_1 (ALU_Op[1], and_6_out, and_7_out);
  or or_2 (or_2_out, and_8_out, and_9_out);
  or or_3 (ALU_Op[0], or_2_out, and_10_out);
endmodule
